// Logisim project bots.circ as structural Verilog: 1 circuit, main circuit main
module main (
  input  CURR_PLAYER,
  input  PREP_PHASE_END,
  input  CLR,
  input  CLK,
  output [3:0] X,
  output [3:0] Y,
  output ROTATED,
  output CONFIRM
);

  wire _10SHIPS, and_2_out, BOOT_PHASE, main_1_out_3, not_1_out, not_2_out, or_1_out, POSITION_CLOCK,
       random_1_out, SHOOT_ONCE_PHASE, undriven;

  Clock clock_1 ();  // open: out
  and and_1 (SHOOT_ONCE_PHASE, CURR_PLAYER, PREP_PHASE_END);
  not not_1 (not_1_out, PREP_PHASE_END);
  not not_2 (not_2_out, _10SHIPS);
  and and_2 (and_2_out, BOOT_PHASE, CLK);
  tick_main main_1 (.in_1(CLK), .in_2(_10SHIPS), .out_3(main_1_out_3));
  or or_1 (or_1_out, main_1_out_3, CLR);
  and and_3 (BOOT_PHASE, not_1_out, not_2_out);
  Counter #(.width(2), .max('h1)) counter_1 (
    .carry(POSITION_CLOCK), .clk(and_2_out), .clr(CONFIRM));  // open: load, D, count, Q
  Counter #(.width(2), .max('h2)) counter_2 (
    .carry(CONFIRM), .clk(and_2_out), .clr(or_1_out));  // open: load, D, count, Q
  Counter #(.width(4), .max('ha), .ongoal("stay")) counter_3 (
    .carry(_10SHIPS), .clk(CONFIRM), .clr(CLR));  // open: load, D, count, Q
  Random #(.width(1)) random_1 (.clk(undriven), .next(undriven), .out(random_1_out));  // open: clr
  Counter #(.width(4), .max('hf)) counter_4 (.Q(Y), .clk(POSITION_CLOCK), .clr(CLR));  // open: load, D, count, carry
  Counter #(.width(1), .max('h1)) counter_5 (
    .Q(ROTATED), .clk(random_1_out), .clr(CLR));  // open: load, D, count, carry

  assign X = 4'b0000;

  // Other names for the same wires on the sheet: CONFIRM_CLOCK = CONFIRM
endmodule
